# Fritzing sketch firegotoBoard-v2 (saved by Fritzing 0.8.7b)
circuit board: 6.58152cm x 9.0621cm

parts:
  DEC = Stepper Motor - Bipolar
  DriverRA = A4988 Stepper Motor Driver Carrier
  DriverDEC = A4988 Stepper Motor Driver Carrier
  C1_DEC = Electrolytic Capacitor [capacitance=1µF package="100 mil [THT, electrolytic]"]
  C2_RA = Electrolytic Capacitor [capacitance=1µF package="100 mil [THT, electrolytic]"]
  J12 = Screw terminal - 2 pins [package=THT]
  RA = Stepper Motor - Bipolar
  Bluetooth = Bluetooth HC-06 Macho
  C3_24V = Electrolytic Capacitor [capacitance=100µF voltage=50V package="100 mil [THT, electrolytic]"]
  C4_VIN = Electrolytic Capacitor [capacitance=100µF voltage=50V package="100 mil [THT, electrolytic]"]
  U1 = Voltage Regulator - 5V [package="TO220 [THT]"]
  LCM1602_IIC1 = LCM1602 IIC [part_number="LCM1602 IIC" chip_label="LCM1602 IIC" package="DIP (Dual Inline) [THT]"]
  Part5 = Thumb Joystick
  S1 = Round Pushbutton
  U2 = POT [package=pot_alpha_rv16af-20]
  S2 = Round Pushbutton
  DriverFoc = A4988 Stepper Motor Driver Carrier
  FOC = Stepper Motor - Bipolar
  C5_FOC = Electrolytic Capacitor [capacitance=1µF package="100 mil [THT, electrolytic]"]
  Part6 = KY-016 RGB Full Color LED Module [package="Breakout board"]
  Part4 = Arduino Due (Rev2b)

nets:
  N1: DEC.A, DriverDEC.OUT_2B
  N2: DEC.C, DriverDEC.OUT_2A
  N3: DEC.B, DriverDEC.OUT_1A
  N4: DEC.D, DriverDEC.OUT_1B
  N5: DriverRA.Enable, Part4.D52
  N6: DriverRA.MS1, Part4.D50
  N7: DriverRA.MS2, Part4.D48
  N8: DriverRA.MS3, Part4.D46
  N9: DriverRA.RESET, Part4.D44
  N10: DriverRA.SLEEP, Part4.D42
  N11: DriverRA.STEP, Part4.D40
  N12: DriverRA.DIR, Part4.D38
  N13: DriverRA.VMOT, DriverDEC.VMOT, C1_DEC.+, C2_RA.+, J12.pin2, C3_24V.+, U1.input_voltage
  GND: DriverRA.GROUND, DriverDEC.GROUND, C1_DEC.-, C2_RA.-, J12.pin1, Bluetooth.GND, C3_24V.-, C4_VIN.-, U1.GND, LCM1602_IIC1.GND, Part5.GND, S1.leg1, U2.E, S2.leg1, DriverFoc.GROUND, C5_FOC.-, Part6.-, Part4.GND
  N14: DriverRA.OUT_2B, RA.A
  N15: DriverRA.OUT_2A, RA.C
  N16: DriverRA.OUT_1A, RA.B
  N17: DriverRA.OUT_1B, RA.D
  N18: DriverDEC.Enable, Part4.D36
  N19: DriverDEC.MS1, Part4.D34
  N20: DriverDEC.MS2, Part4.D32
  N21: DriverDEC.MS3, Part4.D30
  N22: DriverDEC.RESET, Part4.D28
  N23: DriverDEC.SLEEP, Part4.D26
  N24: DriverDEC.STEP, Part4.D24
  N25: DriverDEC.DIR, Part4.D22
  VCC: DriverDEC.VDD, Bluetooth.VCC, LCM1602_IIC1.VCC, Part5.VCC, U2.A, DriverFoc.VDD, Part4.5V
  N26: Bluetooth.TXD, Part4.D15/RX3
  N27: Bluetooth.RXD, Part4.D14/TX3
  N28: C4_VIN.+, U1.output_voltage, Part4.VIN
  N29: LCM1602_IIC1.SDA, Part4.SDA1
  N30: LCM1602_IIC1.SCL, Part4.SCL1
  N31: Part5.SEL, Part4.A2
  N32: Part5.HORZ, Part4.A1
  N33: Part5.VERT, Part4.A0
  N34: S1.leg0, Part4.D25
  N35: U2.S, Part4.A3
  N36: S2.leg0, Part4.D23
  N37: DriverFoc.Enable, Part4.D0/RX
  N38: DriverFoc.MS1, Part4.D1/TX
  N39: DriverFoc.MS2, Part4.D2_PWM
  N40: DriverFoc.MS3, Part4.D3_PWM
  N41: DriverFoc.RESET, Part4.D4_PWM/SS1
  N42: DriverFoc.SLEEP, Part4.D5_PWM
  N43: DriverFoc.STEP, Part4.D6_PWM
  N44: DriverFoc.DIR, Part4.D7_PWM
  N45: DriverFoc.VMOT, C5_FOC.+
  N46: DriverFoc.OUT_2B, FOC.A
  N47: DriverFoc.OUT_2A, FOC.C
  N48: DriverFoc.OUT_1A, FOC.B
  N49: DriverFoc.OUT_1B, FOC.D
  N50: Part6.R, Part4.D53
  N51: Part6.G, Part4.D51
  N52: Part6.B, Part4.D49

notes:
  RA
  DEC
  12V-24V
  -
  B1 B2
  A1 A2
  +
  5V
  FOC

custom parts:
  LCM1602 IIC: I2C-Module to use a 1602 or 2004 LCD on with the wire.h libory Serial LCD Modul
  KY-016 RGB Full Color LED Module: KY-016 Arduino full color 5mm RGB LED, different colors can be obtained by mixing the three primary colors.
